# Fritzing sketch schematic (saved by Fritzing 0.9.3b)

parts:
  U1 = ESP32-38PinWide [part_number=ESP32-38PinWide]
  U2 = SLIDER [package=slider]
  U3 = SLIDER [package=slider]
  Grove1 = Grove OLED 128x96
  Grove2 = Grove OLED 128x96
  Grove3 = Grove OLED 128x96
  Grove4 = Grove OLED 128x96
  Bauteil1 = Adafruit TCA9548A

nets:
  N1: U1.3.3, U2.E
  N2: U1.GPIO36, U2.S
  N3: U1.GPIO39, U3.S
  N4: U1.GND, U2.A
  N5: U1.GPIO21, Bauteil1.INPUTSDA
  N6: U1.GPIO22, Bauteil1.INPUTSCL
  N7: Grove1.SDA, Bauteil1.3SDA
  N8: Grove1.SCL, Bauteil1.2SCL
  N9: Grove2.SDA, Bauteil1.2SDA
  N10: Grove2.SCL, Bauteil1.1SCL
  N11: Grove3.SDA, Bauteil1.1SDA
  N12: Grove3.SCL, Bauteil1.0SCL
  N13: Grove4.SDA, Bauteil1.4SDA
  N14: Grove4.SCL, Bauteil1.3SCL

notes:
  Goes on...
  <--------
  Goes on...

custom parts:
  ESP32-38PinWide: Generic 38-Pin ESP32 with wide format (only access to one side of pins on a breadboard) based on Stephen Lilley's HiLetgo ESP-WROOM-32 ESP32 ESP-32S Development Board.
  Adafruit TCA9548A: You just found the perfect I2C sensor, and you want to wire up two or three or more of them to your Arduino when you realize "Uh oh, this chip has a fixed I2C address, and from what I know about I2C, you cannot have two devices with the same address on the same SDA/SCL pins!" Are you out of luck? You would be, if you didn't have this ultra-cool TCA9548A 1-to-8 I2C multiplexer! Finally, a way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
